# Fritzing sketch raspSketch (saved by Fritzing 0.9.3b)
breadboards: 1

parts:
  U1 = NodeMCU V1.0
  hc-sr2 = hc-sr04
  hc-sr3 = hc-sr04
  hc-sr4 = hc-sr04
  hc-sr5 = hc-sr04
  hc-sr6 = hc-sr04
  Part1 = Arduino Uno (Rev3)
  hc-sr7 = hc-sr04

nets:
  N1: U1.RX, Part1.D1/TX
  N2: U1.TX, Part1.D0/RX
  VCC: hc-sr2.VCC, hc-sr3.VCC, hc-sr4.VCC, hc-sr5.VCC, hc-sr6.VCC, Part1.5V, hc-sr7.VCC
  N3: hc-sr2.Trig, Part1.D6_PWM
  GND: hc-sr2.GND, hc-sr3.GND, hc-sr4.GND, hc-sr5.GND, hc-sr6.GND, Part1.GND
  N4: hc-sr3.Echo, Part1.D12/MISO
  N5: hc-sr4.Trig, Part1.D8
  N6: hc-sr5.Trig, Part1.D9_PWM
  N7: hc-sr6.Trig, Part1.D10_PWM/SS

custom parts:
  NodeMCU V1.0: ESP8266 based NodeMCU
